// Logisim project cpu copy.circ as structural Verilog: 1 circuit, main circuit main
// 1
module main (
  input  [31:0] INSTRUCTION,
  input  CLOCK,
  output [31:0] FETCH_ADDRESS,
  output [31:0] s0_Value,
  output [31:0] s1_Value,
  output [31:0] s2_Value,
  output [31:0] ra_Value,
  output [31:0] sp_Value
);

  wire add, addi, addiu, addu, AluSrc, \and , and_8_out, and_12_out, andi, Beq, Bne, branch, comparator_1_eq,
       comparator_2_eq, comparator_3_eq, comparator_4_eq, comparator_5_eq, comparator_6_eq, comparator_7_eq,
       comparator_8_eq, comparator_9_eq, comparator_10_eq, comparator_19_eq, comparator_20_eq,
       comparator_28_eq, comparator_29_eq, comparator_30_eq, comparator_31_eq, comparator_32_eq,
       comparator_33_eq, comparator_34_eq, comparator_35_eq, comparator_36_eq, comparator_37_eq,
       comparator_38_eq, comparator_39_eq, comparator_40_eq, ctr0, ctr1, ctr2, ctr3, ctr4, ctr5, ctr6, ctr7,
       ctr8, ctr9, ctr10, Extop, J, Jal, jr, Jump, kill, lui, lw, main_2_equal, main_2_signed_overflow,
       main_3_p1, main_3_p2, main_3_p9, main_3_p11, main_3_p13, MemtoReg, MemWrite, \or , ori, RegDst,
       RegWrite, Rtype, sll, slt, slti, sltiu, sltu, sra, Src, srl, sub, subu, sw, swinc;
  wire [3:0] adder_3_out, adder_4_out, adder_5_out, adder_6_out, adder_7_out, adder_8_out, adder_9_out,
       adder_10_out, adder_11_out, bit0, bit1, bit2, bit3, bit4, bit5, bit6, bit7, bit8, bit9, bit10, ctr,
       switch;
  wire [4:0] multiplexer_3_out, multiplexer_4_out, multiplexer_5_out;
  wire [5:0] func, opcode_control;
  wire [25:6] cc_q;
  wire [31:0] adder_2_out, bit_extender_2_out, bit_extender_3_out, bit_extender_4_out, bit_extender_5_out,
       extension, Imm, jp_address, main_1_read_data_2, main_2_result, main_3_p8, multiplexer_1_out,
       multiplexer_2_out, multiplexer_17_out, multiplexer_18_out, multiplexer_19_out, multiplexer_20_out,
       multiplexer_21_out, multiplexer_22_out, PC_4, R1, shift_lui, shifter_1_out, shifter_2_out,
       shifter_3_out;

  Multiplexer #(.width(32)) multiplexer_1 (
    .in0(INSTRUCTION), .in1({32{1'b0}}), .out(multiplexer_1_out), .sel(kill));  // open: en
  Register #(.width(32)) cc (.D(multiplexer_1_out), .Q({opcode_control, cc_q, func}), .clk(CLOCK));  // open: en, clr
  Register #(.width(32)) PC (.D(multiplexer_2_out), .Q(FETCH_ADDRESS), .clk(CLOCK));  // open: en, clr
  Multiplexer #(.width(32)) multiplexer_2 (
    .in0(multiplexer_20_out), .in1(R1), .out(multiplexer_2_out), .sel(jr));  // open: en
  Multiplexer #(.width(5)) multiplexer_3 (
    .in0(cc_q[20:16]), .in1(cc_q[15:11]), .out(multiplexer_3_out), .sel(RegDst));  // open: en
  Comparator #(.width(6)) comparator_1 (.a(opcode_control), .b({6{1'b0}}), .eq(comparator_1_eq));  // open: gt, lt
  Comparator #(.width(6)) comparator_2 (.a(func), .b(6'b100000), .eq(comparator_2_eq));  // open: gt, lt
  Comparator #(.width(6)) comparator_3 (.a(opcode_control), .b({6{1'b0}}), .eq(comparator_3_eq));  // open: gt, lt
  Comparator #(.width(6)) comparator_4 (.a(func), .b(6'b000010), .eq(comparator_4_eq));  // open: gt, lt
  Comparator #(.width(6)) comparator_5 (.a(opcode_control), .b({6{1'b0}}), .eq(comparator_5_eq));  // open: gt, lt
  Comparator #(.width(6)) comparator_6 (.a(func), .b(6'b100011), .eq(comparator_6_eq));  // open: gt, lt
  Comparator #(.width(6)) comparator_7 (.a(opcode_control), .b({6{1'b0}}), .eq(comparator_7_eq));  // open: gt, lt
  Comparator #(.width(6)) comparator_8 (.a(func), .b(6'b100101), .eq(comparator_8_eq));  // open: gt, lt
  Comparator #(.width(6)) comparator_9 (.a(opcode_control), .b({6{1'b0}}), .eq(comparator_9_eq));  // open: gt, lt
  Comparator #(.width(6)) comparator_10 (.a(func), .b(6'b101010), .eq(comparator_10_eq));  // open: gt, lt
  or or_1 (ctr0, sll, lui);
  or or_2 (ctr1, srl, 1'b0);
  or or_3 (ctr2, sra, 1'b0);
  or or_4 (ctr3, add, sw, lw, swinc, addi);
  or or_5 (ctr4, addu, addiu);
  or or_6 (ctr5, sub, 1'b0);
  or or_7 (ctr6, subu, 1'b0);
  or or_8 (ctr7, \and , andi);
  or or_9 (ctr8, \or , ori);
  or or_10 (ctr9, slt, slti);
  or or_11 (ctr10, sltu, sltiu);
  Multiplexer #(.width(5)) multiplexer_4 (
    .in0(multiplexer_5_out), .in1(cc_q[25:21]), .out(multiplexer_4_out), .sel(swinc));  // open: en
  Multiplexer #(.width(5)) multiplexer_5 (
    .in0(multiplexer_3_out), .in1({5{1'b1}}), .out(multiplexer_5_out), .sel(Jal));  // open: en
  Adder #(.width(32)) adder_1 (.a(FETCH_ADDRESS), .b(32'h4), .out(PC_4));  // open: cin, cout
  Comparator #(.width(6), .mode("unsigned")) comparator_11 (
    .a(opcode_control), .b(6'b101011), .eq(sw));  // open: gt, lt
  Comparator #(.width(6), .mode("unsigned")) comparator_12 (
    .a(opcode_control), .b(6'b001000), .eq(addi));  // open: gt, lt
  Comparator #(.width(6), .mode("unsigned")) comparator_13 (
    .a(opcode_control), .b(6'b001001), .eq(addiu));  // open: gt, lt
  Comparator #(.width(6), .mode("unsigned")) comparator_14 (
    .a(opcode_control), .b(6'b001100), .eq(andi));  // open: gt, lt
  Comparator #(.width(6), .mode("unsigned")) comparator_15 (
    .a(opcode_control), .b(6'b001010), .eq(slti));  // open: gt, lt
  Comparator #(.width(6), .mode("unsigned")) comparator_16 (
    .a(opcode_control), .b(6'b001011), .eq(sltiu));  // open: gt, lt
  Comparator #(.width(6), .mode("unsigned")) comparator_17 (
    .a(opcode_control), .b(6'b101100), .eq(swinc));  // open: gt, lt
  Comparator #(.width(6), .mode("unsigned")) comparator_18 (
    .a(opcode_control), .b(6'b001101), .eq(ori));  // open: gt, lt
  Comparator #(.width(6)) comparator_19 (.a(opcode_control), .b({6{1'b0}}), .eq(comparator_19_eq));  // open: gt, lt
  Comparator #(.width(6)) comparator_20 (.a(func), .b(6'b100010), .eq(comparator_20_eq));  // open: gt, lt
  Shifter #(.width(32)) shifter_1 (.in(Imm), .\dist (5'b00010), .out(shifter_1_out));
  Comparator #(.width(6), .mode("unsigned")) comparator_21 (
    .a(opcode_control), .b({6{1'b0}}), .eq(Rtype));  // open: gt, lt
  Comparator #(.width(6), .mode("unsigned")) comparator_22 (
    .a(opcode_control), .b(6'b000100), .eq(Beq));  // open: gt, lt
  Comparator #(.width(6), .mode("unsigned")) comparator_23 (
    .a(opcode_control), .b(6'b000101), .eq(Bne));  // open: gt, lt
  Comparator #(.width(6), .mode("unsigned")) comparator_24 (.a(opcode_control), .b(6'b000010), .eq(J));  // open: gt, lt
  Comparator #(.width(6), .mode("unsigned")) comparator_25 (
    .a(opcode_control), .b(6'b000011), .eq(Jal));  // open: gt, lt
  Comparator #(.width(6), .mode("unsigned")) comparator_26 (
    .a(opcode_control), .b(6'b001111), .eq(lui));  // open: gt, lt
  Comparator #(.width(6), .mode("unsigned")) comparator_27 (
    .a(opcode_control), .b(6'b100011), .eq(lw));  // open: gt, lt
  and and_1 (add, comparator_1_eq, comparator_2_eq);
  and and_2 (sub, comparator_19_eq, comparator_20_eq);
  and and_3 (srl, comparator_3_eq, comparator_4_eq);
  and and_4 (subu, comparator_5_eq, comparator_6_eq);
  and and_5 (\or , comparator_7_eq, comparator_8_eq);
  and and_6 (slt, comparator_9_eq, comparator_10_eq);
  Multiplexer #(.width(4)) multiplexer_6 (.in0(4'b0000), .in1(4'b0000), .out(bit0), .sel(ctr0));  // open: en
  Multiplexer #(.width(4)) multiplexer_7 (.in0(4'b0000), .in1(4'b0001), .out(bit1), .sel(ctr1));  // open: en
  Multiplexer #(.width(4)) multiplexer_8 (.in0(4'b0000), .in1(4'b0010), .out(bit2), .sel(ctr2));  // open: en
  Multiplexer #(.width(4)) multiplexer_9 (.in0(4'b0000), .in1(4'b0011), .out(bit3), .sel(ctr3));  // open: en
  Multiplexer #(.width(4)) multiplexer_10 (.in0(4'b0000), .in1(4'b0100), .out(bit4), .sel(ctr4));  // open: en
  Multiplexer #(.width(4)) multiplexer_11 (.in0(4'b0000), .in1(4'b0101), .out(bit5), .sel(ctr5));  // open: en
  Multiplexer #(.width(4)) multiplexer_12 (.in0(4'b0000), .in1(4'b0110), .out(bit6), .sel(ctr6));  // open: en
  Multiplexer #(.width(4)) multiplexer_13 (.in0(4'b0000), .in1(4'b0111), .out(bit7), .sel(ctr7));  // open: en
  Multiplexer #(.width(4)) multiplexer_14 (.in0(4'b0000), .in1(4'b1000), .out(bit8), .sel(ctr8));  // open: en
  regfile_main main_1 (
    .Read_Register_1(cc_q[25:21]), .Read_Register_2(cc_q[20:16]), .Write_Register(multiplexer_4_out),
    .Write_Data(multiplexer_21_out), .Write_Enable(RegWrite), .Clock(CLOCK), .Read_Data_1(R1),
    .Read_Data_2(main_1_read_data_2), .s0_Value(s0_Value), .s1_Value(s1_Value), .s2_Value(s2_Value),
    .ra_Value(ra_Value), .sp_Value(sp_Value));
  Adder #(.width(32)) adder_2 (.a(shifter_1_out), .b(PC_4), .out(adder_2_out));  // open: cin, cout
  Multiplexer #(.width(4)) multiplexer_15 (.in0(4'b0000), .in1(4'b1001), .out(bit9), .sel(ctr9));  // open: en
  Multiplexer #(.width(4)) multiplexer_16 (.in0(4'b0000), .in1(4'b1001), .out(bit10), .sel(ctr10));  // open: en
  Multiplexer #(.width(32)) multiplexer_17 (
    .in0(R1), .in1(shift_lui), .out(multiplexer_17_out), .sel(Src));  // open: en
  Multiplexer #(.width(32)) multiplexer_18 (
    .in0(main_1_read_data_2), .in1(Imm), .out(multiplexer_18_out), .sel(AluSrc));  // open: en
  Multiplexer #(.width(32)) multiplexer_19 (
    .in0(PC_4), .in1(adder_2_out), .out(multiplexer_19_out), .sel(branch));  // open: en
  Multiplexer #(.width(32)) multiplexer_20 (
    .in0(multiplexer_19_out), .in1(jp_address), .out(multiplexer_20_out), .sel(Jump));  // open: en
  LED sign_overflow (.in(main_2_signed_overflow));
  alu_main main_2 (
    .Switch(switch), .X(multiplexer_17_out), .Equal(main_2_equal), .Result(main_2_result),
    .Signed_Overflow(main_2_signed_overflow), .Y(multiplexer_18_out));
  Comparator #(.width(1), .mode("unsigned")) comparator_28 (
    .a(main_2_equal), .b(1'b0), .eq(comparator_28_eq));  // open: gt, lt
  or or_12 (AluSrc, addi, addiu, slti, sltiu, lui, lw, andi, sw, swinc, ori);
  or or_13 (MemWrite, sw, swinc);
  and and_7 (MemtoReg, lw, 1'b1);
  Comparator #(.width(6)) comparator_29 (.a(opcode_control), .b({6{1'b0}}), .eq(comparator_29_eq));  // open: gt, lt
  Comparator #(.width(6)) comparator_30 (.a(func), .b({6{1'b0}}), .eq(comparator_30_eq));  // open: gt, lt
  Comparator #(.width(6)) comparator_31 (.a(opcode_control), .b({6{1'b0}}), .eq(comparator_31_eq));  // open: gt, lt
  Comparator #(.width(6)) comparator_32 (.a(func), .b(6'b100001), .eq(comparator_32_eq));  // open: gt, lt
  Comparator #(.width(6)) comparator_33 (.a(opcode_control), .b({6{1'b0}}), .eq(comparator_33_eq));  // open: gt, lt
  Comparator #(.width(6)) comparator_34 (.a(func), .b(6'b100100), .eq(comparator_34_eq));  // open: gt, lt
  Comparator #(.width(6)) comparator_35 (.a(opcode_control), .b({6{1'b0}}), .eq(comparator_35_eq));  // open: gt, lt
  Comparator #(.width(6)) comparator_36 (.a(func), .b(6'b000011), .eq(comparator_36_eq));  // open: gt, lt
  Comparator #(.width(6)) comparator_37 (.a(opcode_control), .b({6{1'b0}}), .eq(comparator_37_eq));  // open: gt, lt
  Comparator #(.width(6)) comparator_38 (.a(func), .b(6'b101011), .eq(comparator_38_eq));  // open: gt, lt
  Adder #(.width(4)) adder_3 (.a(bit0), .b(bit1), .out(adder_3_out));  // open: cin, cout
  Adder #(.width(4)) adder_4 (.a(bit4), .b(bit5), .out(adder_4_out));  // open: cin, cout
  and and_8 (and_8_out, main_2_equal, Beq);
  or or_14 (branch, Beq, Bne);
  and and_9 (addu, comparator_31_eq, comparator_32_eq);
  and and_10 (sra, comparator_35_eq, comparator_36_eq);
  and and_11 (sltu, comparator_37_eq, comparator_38_eq);
  Adder #(.width(4)) adder_5 (.a(bit2), .b(bit3), .out(adder_5_out));  // open: cin, cout
  Adder #(.width(4)) adder_6 (.a(bit6), .b(bit7), .out(adder_6_out));  // open: cin, cout
  Adder #(.width(4)) adder_7 (.a(bit8), .b(bit9), .out(adder_7_out));  // open: cin, cout
  // mem_main main_3: pin names not known; wires that end beside it: main_3_p1, main_3_p2, main_2_result, main_1_read_data_2, MemWrite, CLOCK, main_3_p2, main_3_p8, main_3_p9, main_3_p9, main_3_p11, main_3_p11, main_3_p13, main_3_p13
  Multiplexer #(.width(32)) multiplexer_21 (
    .in0(multiplexer_22_out), .in1(PC_4), .out(multiplexer_21_out), .sel(Jal));  // open: en
  and and_12 (and_12_out, comparator_28_eq, Bne);
  or or_15 (RegWrite, addi, addiu, swinc, lw, andi, Jal, ori, slti, sltiu, lui, Rtype);
  and and_13 (sll, comparator_29_eq, comparator_30_eq);
  and and_14 (\and , comparator_33_eq, comparator_34_eq);
  Adder #(.width(4)) adder_8 (.a(adder_3_out), .b(adder_5_out), .out(adder_8_out));  // open: cin, cout
  Adder #(.width(4)) adder_9 (.a(adder_4_out), .b(adder_6_out), .out(adder_9_out));  // open: cin, cout
  Multiplexer #(.width(32)) multiplexer_22 (
    .in0(main_2_result), .in1(main_3_p8), .out(multiplexer_22_out), .sel(MemtoReg));  // open: en
  or or_16 (branch, and_8_out, and_12_out);
  Comparator #(.width(6)) comparator_39 (.a(opcode_control), .b({6{1'b0}}), .eq(comparator_39_eq));  // open: gt, lt
  Comparator #(.width(6)) comparator_40 (.a(func), .b(6'b001000), .eq(comparator_40_eq));  // open: gt, lt
  Multiplexer #(.select(4), .width(4)) multiplexer_23 (
    .in0(4'b0000), .in1(4'b0001), .in2(4'b0010), .in3(4'b0101), .in4(4'b0110), .in5(4'b0111), .in6(4'b1000),
    .in7(4'b1001), .in8(4'b1010), .in9(4'b1011), .in10(4'b1100), .out(switch), .sel(ctr));  // open: in11, in12, in13, in14, in15, en
  Adder #(.width(4)) adder_10 (.a(adder_8_out), .b(adder_9_out), .out(adder_10_out));  // open: cin, cout
  assign extension = {{27{1'b0}}, INSTRUCTION[10:6]};  // Bit_Extender bit_extender_1
  assign bit_extender_2_out = {{16{1'b0}}, INSTRUCTION[15:0]};  // Bit_Extender bit_extender_2
  assign bit_extender_3_out = {{16{INSTRUCTION[15]}}, INSTRUCTION[15:0]};  // Bit_Extender bit_extender_3
  Adder #(.width(4)) adder_11 (.a(adder_10_out), .b(adder_7_out), .out(adder_11_out));  // open: cin, cout
  assign bit_extender_4_out = {{6{1'b0}}, INSTRUCTION[25:0]};  // Bit_Extender bit_extender_4
  assign bit_extender_5_out = {{28{1'b0}}, PC_4[31:28]};  // Bit_Extender bit_extender_5
  or or_17 (kill, Jump, jr, branch);
  Multiplexer #(.width(32)) multiplexer_24 (
    .in0(bit_extender_2_out), .in1(bit_extender_3_out), .out(Imm), .sel(Extop));  // open: en
  or or_18 (Jump, J, Jal);
  and and_15 (jr, comparator_39_eq, comparator_40_eq);
  Adder #(.width(4)) adder_12 (.a(adder_11_out), .b(bit10), .out(ctr));  // open: cin, cout
  Shifter #(.width(32)) shifter_2 (.in(bit_extender_4_out), .\dist (5'b00010), .out(shifter_2_out));
  Shifter #(.width(32)) shifter_3 (.in(bit_extender_5_out), .\dist (5'b11100), .out(shifter_3_out));
  or or_19 (Extop, addi, addiu, slti, sltiu);
  and and_16 (RegDst, Rtype, 1'b1);
  Adder #(.width(32)) adder_13 (.a(shifter_2_out), .b(shifter_3_out), .out(jp_address));  // open: cin, cout
  or or_20 (Src, sll, sra, lui, srl);
  Multiplexer #(.width(32)) multiplexer_25 (.in0(extension), .in1(32'h10), .out(shift_lui), .sel(lui));  // open: en

  // Other names for the same wires on the sheet: clk = CLOCK; fetch_addr[31:0] = FETCH_ADDRESS; ra[31:0] = ra_Value;
  //   s0[31:0] = s0_Value; s1[31:0] = s1_Value; s2[31:0] = s2_Value; sp[31:0] = sp_Value

  // Notes on the sheet:
  //   Output
  //   These are outputs/inputs from run.circ
  //   Inputs
  //   These are DEBUG/TEST outputs from your circuit.
endmodule
