// Logisim project cpu copy.circ as structural Verilog: 1 circuit, main circuit main
// 1
module main (
  input  [31:0] INSTRUCTION,
  input  CLOCK,
  output [31:0] FETCH_ADDRESS,
  output [31:0] s0_Value,
  output [31:0] s1_Value,
  output [31:0] s2_Value,
  output [31:0] ra_Value,
  output [31:0] sp_Value
);

  wire add, addi, addiu, addu, AluSrc, \and , and_19_out, and_23_out, andi, Beq, Bne, branch,
       comparator_1_eq, comparator_2_eq, comparator_3_eq, comparator_4_eq, comparator_5_eq, comparator_6_eq,
       comparator_7_eq, comparator_8_eq, comparator_9_eq, comparator_10_eq, comparator_19_eq,
       comparator_20_eq, comparator_28_eq, comparator_29_eq, comparator_30_eq, comparator_31_eq,
       comparator_32_eq, comparator_33_eq, comparator_34_eq, comparator_35_eq, comparator_36_eq,
       comparator_37_eq, comparator_38_eq, comparator_39_eq, comparator_40_eq, Extop, J, Jal, jr, Jump, lui,
       lw, main_2_equal, main_2_signed_overflow, main_3_p1, main_3_p2, main_3_p9, main_3_p11, main_3_p13,
       MemtoReg, MemWrite, \or , or_1_out, or_2_out, or_3_out, or_4_out, or_5_out, or_6_out, or_7_out,
       or_8_out, or_9_out, or_10_out, or_11_out, or_17_out, ori, RegDst, RegWrite, Rtype, sll, slt, slti,
       sltiu, sltu, sra, Src, srl, sub, subu, sw, swinc;
  wire [3:0] and_7_out, and_8_out, and_9_out, and_10_out, and_11_out, and_12_out, and_13_out, and_14_out,
       and_15_out, and_16_out, and_17_out, bit_extender_1_out, bit_extender_2_out, bit_extender_3_out,
       bit_extender_4_out, bit_extender_5_out, bit_extender_6_out, bit_extender_7_out, bit_extender_8_out,
       bit_extender_9_out, bit_extender_10_out, bit_extender_11_out, switch;
  wire [4:0] multiplexer_2_out, multiplexer_3_out, multiplexer_4_out;
  wire [31:0] adder_2_out, bit_extender_13_out, bit_extender_14_out, bit_extender_15_out,
       bit_extender_16_out, extension, Imm, jp_address, main_1_read_data_2, main_2_result, main_3_p8,
       multiplexer_1_out, multiplexer_5_out, multiplexer_6_out, multiplexer_7_out, multiplexer_8_out,
       multiplexer_9_out, multiplexer_10_out, multiplexer_11_out, PC_4, R1, shift_lui, shifter_1_out,
       shifter_2_out, shifter_3_out, swinc_val;

  Register #(.width(32)) PC (.D(multiplexer_1_out), .Q(FETCH_ADDRESS), .clk(CLOCK));  // open: en, clr
  Multiplexer #(.width(32)) multiplexer_1 (
    .in0(multiplexer_6_out), .in1(R1), .out(multiplexer_1_out), .en(jr));  // open: sel
  Multiplexer #(.width(5)) multiplexer_2 (
    .in0(INSTRUCTION[20:16]), .in1(INSTRUCTION[15:11]), .out(multiplexer_2_out), .sel(RegDst));  // open: en
  Comparator #(.width(6)) comparator_1 (.a(INSTRUCTION[31:26]), .b({6{1'b0}}), .eq(comparator_1_eq));  // open: gt, lt
  Comparator #(.width(6)) comparator_2 (.a(INSTRUCTION[5:0]), .b(6'b100000), .eq(comparator_2_eq));  // open: gt, lt
  Comparator #(.width(6)) comparator_3 (.a(INSTRUCTION[31:26]), .b({6{1'b0}}), .eq(comparator_3_eq));  // open: gt, lt
  Comparator #(.width(6)) comparator_4 (.a(INSTRUCTION[5:0]), .b(6'b000010), .eq(comparator_4_eq));  // open: gt, lt
  Comparator #(.width(6)) comparator_5 (.a(INSTRUCTION[31:26]), .b({6{1'b0}}), .eq(comparator_5_eq));  // open: gt, lt
  Comparator #(.width(6)) comparator_6 (.a(INSTRUCTION[5:0]), .b(6'b100011), .eq(comparator_6_eq));  // open: gt, lt
  Comparator #(.width(6)) comparator_7 (.a(INSTRUCTION[31:26]), .b({6{1'b0}}), .eq(comparator_7_eq));  // open: gt, lt
  Comparator #(.width(6)) comparator_8 (.a(INSTRUCTION[5:0]), .b(6'b100101), .eq(comparator_8_eq));  // open: gt, lt
  Comparator #(.width(6)) comparator_9 (.a(INSTRUCTION[31:26]), .b({6{1'b0}}), .eq(comparator_9_eq));  // open: gt, lt
  Comparator #(.width(6)) comparator_10 (.a(INSTRUCTION[5:0]), .b(6'b101010), .eq(comparator_10_eq));  // open: gt, lt
  or or_1 (or_1_out, sll, lui);
  or or_2 (or_2_out, srl, 1'b0);
  or or_3 (or_3_out, sra, 1'b0);
  or or_4 (or_4_out, add, sw, lw, swinc, addi);
  or or_5 (or_5_out, addu, addiu);
  or or_6 (or_6_out, sub, 1'b0);
  or or_7 (or_7_out, subu, 1'b0);
  or or_8 (or_8_out, \and , andi);
  or or_9 (or_9_out, \or , ori);
  or or_10 (or_10_out, slt, slti);
  or or_11 (or_11_out, sltu, sltiu);
  Multiplexer #(.width(5)) multiplexer_3 (
    .in0(multiplexer_4_out), .in1(INSTRUCTION[25:21]), .out(multiplexer_3_out), .sel(swinc));  // open: en
  Multiplexer #(.width(5)) multiplexer_4 (
    .in0(multiplexer_2_out), .in1({5{1'b1}}), .out(multiplexer_4_out), .sel(Jal));  // open: en
  Adder #(.width(32)) adder_1 (.a(FETCH_ADDRESS), .b(32'h4), .out(PC_4));  // open: cin, cout
  Comparator #(.width(6), .mode("unsigned")) comparator_11 (
    .a(INSTRUCTION[31:26]), .b(6'b101011), .eq(sw));  // open: gt, lt
  Comparator #(.width(6), .mode("unsigned")) comparator_12 (
    .a(INSTRUCTION[31:26]), .b(6'b001000), .eq(addi));  // open: gt, lt
  Comparator #(.width(6), .mode("unsigned")) comparator_13 (
    .a(INSTRUCTION[31:26]), .b(6'b001001), .eq(addiu));  // open: gt, lt
  Comparator #(.width(6), .mode("unsigned")) comparator_14 (
    .a(INSTRUCTION[31:26]), .b(6'b001100), .eq(andi));  // open: gt, lt
  Comparator #(.width(6), .mode("unsigned")) comparator_15 (
    .a(INSTRUCTION[31:26]), .b(6'b001010), .eq(slti));  // open: gt, lt
  Comparator #(.width(6), .mode("unsigned")) comparator_16 (
    .a(INSTRUCTION[31:26]), .b(6'b001011), .eq(sltiu));  // open: gt, lt
  Comparator #(.width(6), .mode("unsigned")) comparator_17 (
    .a(INSTRUCTION[31:26]), .b(6'b101100), .eq(swinc));  // open: gt, lt
  Comparator #(.width(6), .mode("unsigned")) comparator_18 (
    .a(INSTRUCTION[31:26]), .b(6'b001101), .eq(ori));  // open: gt, lt
  Comparator #(.width(6)) comparator_19 (.a(INSTRUCTION[31:26]), .b({6{1'b0}}), .eq(comparator_19_eq));  // open: gt, lt
  Comparator #(.width(6)) comparator_20 (.a(INSTRUCTION[5:0]), .b(6'b100010), .eq(comparator_20_eq));  // open: gt, lt
  assign bit_extender_1_out = {{3{1'b0}}, or_1_out};  // Bit_Extender bit_extender_1
  assign bit_extender_2_out = {{3{1'b0}}, or_2_out};  // Bit_Extender bit_extender_2
  assign bit_extender_3_out = {{3{1'b0}}, or_3_out};  // Bit_Extender bit_extender_3
  assign bit_extender_4_out = {{3{1'b0}}, or_4_out};  // Bit_Extender bit_extender_4
  assign bit_extender_5_out = {{3{1'b0}}, or_5_out};  // Bit_Extender bit_extender_5
  assign bit_extender_6_out = {{3{1'b0}}, or_6_out};  // Bit_Extender bit_extender_6
  assign bit_extender_7_out = {{3{1'b0}}, or_7_out};  // Bit_Extender bit_extender_7
  assign bit_extender_8_out = {{3{1'b0}}, or_8_out};  // Bit_Extender bit_extender_8
  assign bit_extender_9_out = {{3{1'b0}}, or_9_out};  // Bit_Extender bit_extender_9
  assign bit_extender_10_out = {{3{1'b0}}, or_10_out};  // Bit_Extender bit_extender_10
  assign bit_extender_11_out = {{3{1'b0}}, or_11_out};  // Bit_Extender bit_extender_11
  Shifter #(.width(32)) shifter_1 (.in(Imm), .\dist (5'b00010), .out(shifter_1_out));
  Comparator #(.width(6), .mode("unsigned")) comparator_21 (
    .a(INSTRUCTION[31:26]), .b({6{1'b0}}), .eq(Rtype));  // open: gt, lt
  Comparator #(.width(6), .mode("unsigned")) comparator_22 (
    .a(INSTRUCTION[31:26]), .b(6'b000100), .eq(Beq));  // open: gt, lt
  Comparator #(.width(6), .mode("unsigned")) comparator_23 (
    .a(INSTRUCTION[31:26]), .b(6'b000101), .eq(Bne));  // open: gt, lt
  Comparator #(.width(6), .mode("unsigned")) comparator_24 (
    .a(INSTRUCTION[31:26]), .b(6'b000010), .eq(J));  // open: gt, lt
  Comparator #(.width(6), .mode("unsigned")) comparator_25 (
    .a(INSTRUCTION[31:26]), .b(6'b000011), .eq(Jal));  // open: gt, lt
  Comparator #(.width(6), .mode("unsigned")) comparator_26 (
    .a(INSTRUCTION[31:26]), .b(6'b001111), .eq(lui));  // open: gt, lt
  Comparator #(.width(6), .mode("unsigned")) comparator_27 (
    .a(INSTRUCTION[31:26]), .b(6'b100011), .eq(lw));  // open: gt, lt
  and and_1 (add, comparator_1_eq, comparator_2_eq);
  and and_2 (sub, comparator_19_eq, comparator_20_eq);
  and and_3 (srl, comparator_3_eq, comparator_4_eq);
  and and_4 (subu, comparator_5_eq, comparator_6_eq);
  and and_5 (\or , comparator_7_eq, comparator_8_eq);
  and and_6 (slt, comparator_9_eq, comparator_10_eq);
  assign and_7_out = bit_extender_1_out & 4'b0000;  // AND_Gate and_7, 4 bits wide
  assign and_8_out = bit_extender_2_out & 4'b0001;  // AND_Gate and_8, 4 bits wide
  assign and_9_out = bit_extender_3_out & 4'b0010;  // AND_Gate and_9, 4 bits wide
  assign and_10_out = bit_extender_4_out & 4'b0101;  // AND_Gate and_10, 4 bits wide
  assign and_11_out = bit_extender_5_out & 4'b0110;  // AND_Gate and_11, 4 bits wide
  assign and_12_out = bit_extender_6_out & 4'b0111;  // AND_Gate and_12, 4 bits wide
  assign and_13_out = bit_extender_7_out & 4'b1000;  // AND_Gate and_13, 4 bits wide
  assign and_14_out = bit_extender_8_out & 4'b1001;  // AND_Gate and_14, 4 bits wide
  assign and_15_out = bit_extender_9_out & 4'b1010;  // AND_Gate and_15, 4 bits wide
  assign and_16_out = bit_extender_10_out & 4'b1011;  // AND_Gate and_16, 4 bits wide
  assign and_17_out = bit_extender_11_out & 4'b1100;  // AND_Gate and_17, 4 bits wide
  regfile_main main_1 (
    .Read_Register_1(INSTRUCTION[25:21]), .Read_Register_2(INSTRUCTION[20:16]),
    .Write_Register(multiplexer_3_out), .Write_Data(multiplexer_5_out), .Write_Enable(RegWrite),
    .Clock(CLOCK), .Read_Data_1(R1), .Read_Data_2(main_1_read_data_2), .s0_Value(s0_Value),
    .s1_Value(s1_Value), .s2_Value(s2_Value), .ra_Value(ra_Value), .sp_Value(sp_Value));
  Multiplexer #(.width(32)) multiplexer_5 (
    .in0(multiplexer_10_out), .in1(PC_4), .out(multiplexer_5_out), .en(Jal));  // open: sel
  Adder #(.width(32)) adder_2 (.a(shifter_1_out), .b(PC_4), .out(adder_2_out));  // open: cin, cout
  Multiplexer #(.width(32)) multiplexer_6 (
    .in0(multiplexer_9_out), .in1(jp_address), .out(multiplexer_6_out), .en(Jump));  // open: sel
  Multiplexer #(.width(32)) multiplexer_7 (.in0(R1), .in1(shift_lui), .out(multiplexer_7_out), .sel(Src));  // open: en
  Multiplexer #(.width(32)) multiplexer_8 (
    .in0(main_1_read_data_2), .in1(Imm), .out(multiplexer_8_out), .sel(AluSrc));  // open: en
  Multiplexer #(.width(32)) multiplexer_9 (
    .in0(PC_4), .in1(adder_2_out), .out(multiplexer_9_out), .sel(or_17_out));  // open: en
  LED sign_overflow (.in(main_2_signed_overflow));
  alu_main main_2 (
    .Switch(switch), .X(multiplexer_7_out), .Equal(main_2_equal), .Result(main_2_result),
    .Signed_Overflow(main_2_signed_overflow), .Y(multiplexer_8_out));
  assign switch = and_7_out | and_8_out | and_9_out | and_10_out | and_11_out | and_12_out | and_13_out | and_14_out | and_15_out | and_16_out | and_17_out;  // OR_Gate or_12, 4 bits wide
  Multiplexer #(.width(32)) multiplexer_10 (
    .in0(multiplexer_11_out), .in1(swinc_val), .out(multiplexer_10_out), .en(swinc));  // open: sel
  Comparator #(.width(1), .mode("unsigned")) comparator_28 (
    .a(main_2_equal), .b(1'b0), .eq(comparator_28_eq));  // open: gt, lt
  or or_13 (AluSrc, addi, addiu, slti, sltiu, lui, lw, andi, sw, swinc, ori);
  or or_14 (MemWrite, sw, swinc);
  and and_18 (MemtoReg, lw, 1'b1);
  Comparator #(.width(6)) comparator_29 (.a(INSTRUCTION[31:26]), .b({6{1'b0}}), .eq(comparator_29_eq));  // open: gt, lt
  Comparator #(.width(6)) comparator_30 (.a(INSTRUCTION[5:0]), .b({6{1'b0}}), .eq(comparator_30_eq));  // open: gt, lt
  Comparator #(.width(6)) comparator_31 (.a(INSTRUCTION[31:26]), .b({6{1'b0}}), .eq(comparator_31_eq));  // open: gt, lt
  Comparator #(.width(6)) comparator_32 (.a(INSTRUCTION[5:0]), .b(6'b100001), .eq(comparator_32_eq));  // open: gt, lt
  Comparator #(.width(6)) comparator_33 (.a(INSTRUCTION[31:26]), .b({6{1'b0}}), .eq(comparator_33_eq));  // open: gt, lt
  Comparator #(.width(6)) comparator_34 (.a(INSTRUCTION[5:0]), .b(6'b100100), .eq(comparator_34_eq));  // open: gt, lt
  Comparator #(.width(6)) comparator_35 (.a(INSTRUCTION[31:26]), .b({6{1'b0}}), .eq(comparator_35_eq));  // open: gt, lt
  Comparator #(.width(6)) comparator_36 (.a(INSTRUCTION[5:0]), .b(6'b000011), .eq(comparator_36_eq));  // open: gt, lt
  Comparator #(.width(6)) comparator_37 (.a(INSTRUCTION[31:26]), .b({6{1'b0}}), .eq(comparator_37_eq));  // open: gt, lt
  Comparator #(.width(6)) comparator_38 (.a(INSTRUCTION[5:0]), .b(6'b101011), .eq(comparator_38_eq));  // open: gt, lt
  and and_19 (and_19_out, main_2_equal, Beq);
  or or_15 (branch, Beq, Bne);
  and and_20 (addu, comparator_31_eq, comparator_32_eq);
  and and_21 (sra, comparator_35_eq, comparator_36_eq);
  and and_22 (sltu, comparator_37_eq, comparator_38_eq);
  // mem_main main_3: pin names not known; wires that end beside it: main_3_p1, main_3_p2, main_2_result, main_1_read_data_2, MemWrite, CLOCK, main_3_p2, main_3_p8, main_3_p9, main_3_p9, main_3_p11, main_3_p11, main_3_p13, main_3_p13
  and and_23 (and_23_out, comparator_28_eq, Bne);
  or or_16 (RegWrite, addi, addiu, swinc, lw, andi, Jal, ori, slti, sltiu, lui, Rtype);
  and and_24 (sll, comparator_29_eq, comparator_30_eq);
  and and_25 (\and , comparator_33_eq, comparator_34_eq);
  Multiplexer #(.width(32)) multiplexer_11 (
    .in0(main_2_result), .in1(main_3_p8), .out(multiplexer_11_out), .sel(MemtoReg));  // open: en
  or or_17 (or_17_out, and_19_out, and_23_out);
  Comparator #(.width(6)) comparator_39 (.a(INSTRUCTION[31:26]), .b({6{1'b0}}), .eq(comparator_39_eq));  // open: gt, lt
  Comparator #(.width(6)) comparator_40 (.a(INSTRUCTION[5:0]), .b(6'b001000), .eq(comparator_40_eq));  // open: gt, lt
  assign extension = {{27{1'b0}}, INSTRUCTION[10:6]};  // Bit_Extender bit_extender_12
  assign bit_extender_13_out = {{16{1'b0}}, INSTRUCTION[15:0]};  // Bit_Extender bit_extender_13
  assign bit_extender_14_out = {{16{INSTRUCTION[15]}}, INSTRUCTION[15:0]};  // Bit_Extender bit_extender_14
  assign bit_extender_15_out = {{6{1'b0}}, INSTRUCTION[25:0]};  // Bit_Extender bit_extender_15
  assign bit_extender_16_out = {{28{1'b0}}, PC_4[31:28]};  // Bit_Extender bit_extender_16
  Adder #(.width(32)) adder_3 (.a(R1), .b(Imm), .out(swinc_val));  // open: cin, cout
  Multiplexer #(.width(32)) multiplexer_12 (
    .in0(bit_extender_13_out), .in1(bit_extender_14_out), .out(Imm), .sel(Extop));  // open: en
  or or_18 (Jump, J, Jal);
  and and_26 (jr, comparator_39_eq, comparator_40_eq);
  Shifter #(.width(32)) shifter_2 (.in(bit_extender_15_out), .\dist (5'b00010), .out(shifter_2_out));
  Shifter #(.width(32)) shifter_3 (.in(bit_extender_16_out), .\dist (5'b11100), .out(shifter_3_out));
  or or_19 (Extop, addi, addiu, slti, sltiu);
  and and_27 (RegDst, Rtype, 1'b1);
  Adder #(.width(32)) adder_4 (.a(shifter_2_out), .b(shifter_3_out), .out(jp_address));  // open: cin, cout
  or or_20 (Src, sll, sra, lui, srl);
  Multiplexer #(.width(32)) multiplexer_13 (.in0(extension), .in1(32'hf), .out(shift_lui), .sel(lui));  // open: en

  // Other names for the same wires on the sheet: clk = CLOCK; fetch_addr[31:0] = FETCH_ADDRESS;
  //   func[5:0] = INSTRUCTION[5:0]; opcode_control[5:0] = INSTRUCTION[31:26]; ra[31:0] = ra_Value;
  //   s0[31:0] = s0_Value; s1[31:0] = s1_Value; s2[31:0] = s2_Value; sp[31:0] = sp_Value

  // Notes on the sheet:
  //   Output
  //   These are outputs/inputs from run.circ
  //   Inputs
  //   These are DEBUG/TEST outputs from your circuit.
endmodule
