// Logisim project cpu.circ as structural Verilog: 1 circuit, main circuit main
// 1
module main (
  input  [31:0] INSTRUCTION,
  input  CLOCK,
  output [31:0] FETCH_ADDRESS,
  output [31:0] s0_Value,
  output [31:0] s1_Value,
  output [31:0] s2_Value,
  output [31:0] ra_Value,
  output [31:0] sp_Value
);

  wire add, addi, addiu, addu, AluSrc, \and , and_8_out, and_10_out, andi, Beq, Bne, branch, comparator_1_eq,
       comparator_2_eq, comparator_3_eq, comparator_4_eq, comparator_5_eq, comparator_6_eq, comparator_7_eq,
       comparator_8_eq, comparator_9_eq, comparator_10_eq, comparator_11_eq, comparator_12_eq,
       comparator_28_eq, comparator_29_eq, comparator_30_eq, comparator_31_eq, comparator_32_eq,
       comparator_33_eq, comparator_34_eq, comparator_35_eq, comparator_36_eq, comparator_37_eq,
       comparator_38_eq, comparator_39_eq, comparator_40_eq, ctr0, ctr1, ctr2, ctr3, ctr4, ctr5, ctr6, ctr7,
       ctr8, ctr9, ctr10, Extop, J, Jal, jr, Jump, kill, lui, lw, main_2_equal, main_2_signed_overflow,
       MemtoReg, MemWrite, \or , ori, RegDst, RegWrite, Rtype, sll, slt, slti, sltiu, sltu, sra, Src, srl,
       sub, subu, sw, swinc;
  wire [3:0] adder_2_out, adder_3_out, adder_4_out, adder_5_out, adder_6_out, adder_7_out, adder_8_out,
       adder_9_out, adder_10_out, bit0, bit1, bit2, bit3, bit4, bit5, bit6, bit7, bit8, bit9, bit10, ctr,
       switch;
  wire [4:0] multiplexer_22_out, multiplexer_24_out, write_reg;
  wire [31:0] actual_instruction, adder_1_out, bit_extender_2_out, bit_extender_3_out, bit_extender_4_out,
       bit_extender_5_out, branchTo, extension, Imm, jp_address, main_1_read_data_2, main_2_result,
       main_3_p5, multiplexer_1_out, multiplexer_13_out, multiplexer_14_out, multiplexer_15_out,
       multiplexer_16_out, multiplexer_18_out, multiplexer_19_out, multiplexer_20_out, r1, shift_lui,
       shifter_1_out, shifter_2_out, shifter_3_out;

  Register #(.width(32)) PC (.D(multiplexer_18_out), .Q(FETCH_ADDRESS), .clk(CLOCK));  // open: en, clr
  // Probe on INSTRUCTION
  or or_1 (Src, sll, sra, lui, srl);
  Comparator #(.width(6)) comparator_1 (
    .a(actual_instruction[31:26]), .b({6{1'b0}}), .eq(comparator_1_eq));  // open: gt, lt
  Comparator #(.width(6)) comparator_2 (
    .a(actual_instruction[5:0]), .b(6'b100000), .eq(comparator_2_eq));  // open: gt, lt
  Comparator #(.width(6)) comparator_3 (
    .a(actual_instruction[31:26]), .b({6{1'b0}}), .eq(comparator_3_eq));  // open: gt, lt
  Comparator #(.width(6)) comparator_4 (
    .a(actual_instruction[5:0]), .b(6'b100010), .eq(comparator_4_eq));  // open: gt, lt
  Comparator #(.width(6)) comparator_5 (
    .a(actual_instruction[31:26]), .b({6{1'b0}}), .eq(comparator_5_eq));  // open: gt, lt
  Comparator #(.width(6)) comparator_6 (
    .a(actual_instruction[5:0]), .b(6'b000010), .eq(comparator_6_eq));  // open: gt, lt
  Comparator #(.width(6)) comparator_7 (
    .a(actual_instruction[31:26]), .b({6{1'b0}}), .eq(comparator_7_eq));  // open: gt, lt
  Comparator #(.width(6)) comparator_8 (
    .a(actual_instruction[5:0]), .b(6'b100011), .eq(comparator_8_eq));  // open: gt, lt
  Comparator #(.width(6)) comparator_9 (
    .a(actual_instruction[31:26]), .b({6{1'b0}}), .eq(comparator_9_eq));  // open: gt, lt
  Comparator #(.width(6)) comparator_10 (
    .a(actual_instruction[5:0]), .b(6'b100101), .eq(comparator_10_eq));  // open: gt, lt
  Comparator #(.width(6)) comparator_11 (
    .a(actual_instruction[31:26]), .b({6{1'b0}}), .eq(comparator_11_eq));  // open: gt, lt
  Comparator #(.width(6)) comparator_12 (
    .a(actual_instruction[5:0]), .b(6'b101010), .eq(comparator_12_eq));  // open: gt, lt
  or or_2 (ctr0, sll, lui);
  or or_3 (ctr7, \and , andi);
  or or_4 (ctr8, \or , ori);
  or or_5 (ctr9, slt, slti);
  or or_6 (ctr10, sltu, sltiu);
  // Probe on actual_instruction[25:21]
  // Probe on actual_instruction[20:16]
  // Probe on write_reg
  Comparator #(.width(6), .mode("unsigned")) comparator_13 (
    .a(actual_instruction[31:26]), .b(6'b000011), .eq(Jal));  // open: gt, lt
  Comparator #(.width(6), .mode("unsigned")) comparator_14 (
    .a(actual_instruction[31:26]), .b(6'b001111), .eq(lui));  // open: gt, lt
  Comparator #(.width(6), .mode("unsigned")) comparator_15 (
    .a(actual_instruction[31:26]), .b(6'b100011), .eq(lw));  // open: gt, lt
  Comparator #(.width(6), .mode("unsigned")) comparator_16 (
    .a(actual_instruction[31:26]), .b(6'b101011), .eq(sw));  // open: gt, lt
  Comparator #(.width(6), .mode("unsigned")) comparator_17 (
    .a(actual_instruction[31:26]), .b(6'b001000), .eq(addi));  // open: gt, lt
  Comparator #(.width(6), .mode("unsigned")) comparator_18 (
    .a(actual_instruction[31:26]), .b(6'b001001), .eq(addiu));  // open: gt, lt
  Comparator #(.width(6), .mode("unsigned")) comparator_19 (
    .a(actual_instruction[31:26]), .b(6'b001100), .eq(andi));  // open: gt, lt
  Comparator #(.width(6), .mode("unsigned")) comparator_20 (
    .a(actual_instruction[31:26]), .b(6'b001010), .eq(slti));  // open: gt, lt
  Comparator #(.width(6), .mode("unsigned")) comparator_21 (
    .a(actual_instruction[31:26]), .b(6'b001011), .eq(sltiu));  // open: gt, lt
  Comparator #(.width(6), .mode("unsigned")) comparator_22 (
    .a(actual_instruction[31:26]), .b(6'b101100), .eq(swinc));  // open: gt, lt
  Comparator #(.width(6), .mode("unsigned")) comparator_23 (
    .a(actual_instruction[31:26]), .b(6'b001101), .eq(ori));  // open: gt, lt
  and and_1 (add, comparator_1_eq, comparator_2_eq);
  or or_7 (ctr1, srl, 1'b0);
  or or_8 (ctr2, sra, 1'b0);
  or or_9 (ctr3, add, sw, lw, swinc, addi);
  or or_10 (ctr4, addu, addiu);
  or or_11 (ctr5, sub, 1'b0);
  or or_12 (ctr6, subu, 1'b0);
  Adder #(.width(32)) adder_1 (.a(FETCH_ADDRESS), .b(32'h4), .out(adder_1_out));  // open: cin, cout
  // Probe on adder_1_out
  Multiplexer #(.width(32)) multiplexer_1 (
    .in0(INSTRUCTION), .in1({32{1'b0}}), .out(multiplexer_1_out), .sel(kill));  // open: en
  // Probe on RegWrite
  Comparator #(.width(6), .mode("unsigned")) comparator_24 (
    .a(actual_instruction[31:26]), .b({6{1'b0}}), .eq(Rtype));  // open: gt, lt
  Comparator #(.width(6), .mode("unsigned")) comparator_25 (
    .a(actual_instruction[31:26]), .b(6'b000100), .eq(Beq));  // open: gt, lt
  Comparator #(.width(6), .mode("unsigned")) comparator_26 (
    .a(actual_instruction[31:26]), .b(6'b000101), .eq(Bne));  // open: gt, lt
  Comparator #(.width(6), .mode("unsigned")) comparator_27 (
    .a(actual_instruction[31:26]), .b(6'b000010), .eq(J));  // open: gt, lt
  and and_2 (sub, comparator_3_eq, comparator_4_eq);
  and and_3 (srl, comparator_5_eq, comparator_6_eq);
  and and_4 (subu, comparator_7_eq, comparator_8_eq);
  and and_5 (\or , comparator_9_eq, comparator_10_eq);
  and and_6 (slt, comparator_11_eq, comparator_12_eq);
  Multiplexer #(.width(4)) multiplexer_2 (.in0(4'b0000), .in1(4'b0000), .out(bit0), .sel(ctr0));  // open: en
  Multiplexer #(.width(4)) multiplexer_3 (.in0(4'b0000), .in1(4'b0110), .out(bit6), .sel(ctr6));  // open: en
  Multiplexer #(.width(4)) multiplexer_4 (.in0(4'b0000), .in1(4'b0111), .out(bit7), .sel(ctr7));  // open: en
  Multiplexer #(.width(4)) multiplexer_5 (.in0(4'b0000), .in1(4'b1000), .out(bit8), .sel(ctr8));  // open: en
  Multiplexer #(.width(4)) multiplexer_6 (.in0(4'b0000), .in1(4'b1001), .out(bit9), .sel(ctr9));  // open: en
  Multiplexer #(.width(4)) multiplexer_7 (.in0(4'b0000), .in1(4'b1010), .out(bit10), .sel(ctr10));  // open: en
  Register #(.width(32)) pipeline (.D(multiplexer_1_out), .Q(actual_instruction), .clk(CLOCK));  // open: en, clr
  // Probe on actual_instruction
  regfile_main main_1 (
    .Read_Register_1(actual_instruction[25:21]), .Read_Register_2(actual_instruction[20:16]),
    .Write_Register(write_reg), .Write_Data(multiplexer_20_out), .Write_Enable(RegWrite), .Clock(CLOCK),
    .Read_Data_1(r1), .Read_Data_2(main_1_read_data_2), .s0_Value(s0_Value), .s1_Value(s1_Value),
    .s2_Value(s2_Value), .ra_Value(ra_Value), .sp_Value(sp_Value));
  or or_13 (Jump, J, Jal);
  Multiplexer #(.width(4)) multiplexer_8 (.in0(4'b0000), .in1(4'b0001), .out(bit1), .sel(ctr1));  // open: en
  Multiplexer #(.width(4)) multiplexer_9 (.in0(4'b0000), .in1(4'b0010), .out(bit2), .sel(ctr2));  // open: en
  Multiplexer #(.width(4)) multiplexer_10 (.in0(4'b0000), .in1(4'b0011), .out(bit3), .sel(ctr3));  // open: en
  Multiplexer #(.width(4)) multiplexer_11 (.in0(4'b0000), .in1(4'b0100), .out(bit4), .sel(ctr4));  // open: en
  Multiplexer #(.width(4)) multiplexer_12 (.in0(4'b0000), .in1(4'b0101), .out(bit5), .sel(ctr5));  // open: en
  Multiplexer #(.width(32)) multiplexer_13 (
    .in0(r1), .in1(shift_lui), .out(multiplexer_13_out), .sel(Src));  // open: en
  Multiplexer #(.width(32)) multiplexer_14 (
    .in0(main_1_read_data_2), .in1(Imm), .out(multiplexer_14_out), .sel(AluSrc));  // open: en
  Multiplexer #(.width(32)) multiplexer_15 (
    .in0(adder_1_out), .in1(branchTo), .out(multiplexer_15_out), .sel(branch));  // open: en
  LED sign_overflow (.in(main_2_signed_overflow));
  alu_main main_2 (
    .Switch(switch), .X(multiplexer_13_out), .Equal(main_2_equal), .Result(main_2_result),
    .Signed_Overflow(main_2_signed_overflow), .Y(multiplexer_14_out));
  // Probe on multiplexer_14_out
  // Probe on multiplexer_20_out
  or or_14 (MemWrite, sw, swinc);
  and and_7 (MemtoReg, lw, 1'b1);
  // Probe on main_2_result
  or or_15 (AluSrc, addi, addiu, slti, sltiu, lui, lw, andi, sw, swinc, ori);
  Comparator #(.width(6)) comparator_28 (
    .a(actual_instruction[31:26]), .b({6{1'b0}}), .eq(comparator_28_eq));  // open: gt, lt
  Comparator #(.width(6)) comparator_29 (
    .a(actual_instruction[5:0]), .b({6{1'b0}}), .eq(comparator_29_eq));  // open: gt, lt
  Comparator #(.width(6)) comparator_30 (
    .a(actual_instruction[31:26]), .b({6{1'b0}}), .eq(comparator_30_eq));  // open: gt, lt
  Comparator #(.width(6)) comparator_31 (
    .a(actual_instruction[5:0]), .b(6'b100001), .eq(comparator_31_eq));  // open: gt, lt
  // Probe on switch
  Multiplexer #(.width(32)) multiplexer_16 (
    .in0(multiplexer_15_out), .in1(jp_address), .out(multiplexer_16_out), .sel(Jump));  // open: en
  and and_8 (and_8_out, main_2_equal, Beq);
  Comparator #(.width(1), .mode("unsigned")) comparator_32 (
    .a(main_2_equal), .b(1'b0), .eq(comparator_32_eq));  // open: gt, lt
  // mem_main main_3: pin names not known; wires that end beside it: main_2_result, main_1_read_data_2, MemWrite, CLOCK, main_3_p5
  // Probe on Jal
  assign extension = {{27{1'b0}}, actual_instruction[10:6]};  // Bit_Extender bit_extender_1
  assign bit_extender_2_out = {{16{1'b0}}, actual_instruction[15:0]};  // Bit_Extender bit_extender_2
  assign bit_extender_3_out = {{16{actual_instruction[15]}}, actual_instruction[15:0]};  // Bit_Extender bit_extender_3
  Multiplexer #(.width(32)) multiplexer_17 (.in0(extension), .in1(32'h10), .out(shift_lui), .sel(lui));  // open: en
  and and_9 (sll, comparator_28_eq, comparator_29_eq);
  Comparator #(.width(6)) comparator_33 (
    .a(actual_instruction[31:26]), .b({6{1'b0}}), .eq(comparator_33_eq));  // open: gt, lt
  Comparator #(.width(6)) comparator_34 (
    .a(actual_instruction[5:0]), .b(6'b100100), .eq(comparator_34_eq));  // open: gt, lt
  Comparator #(.width(6)) comparator_35 (
    .a(actual_instruction[31:26]), .b({6{1'b0}}), .eq(comparator_35_eq));  // open: gt, lt
  Comparator #(.width(6)) comparator_36 (
    .a(actual_instruction[5:0]), .b(6'b000011), .eq(comparator_36_eq));  // open: gt, lt
  Adder #(.width(4)) adder_2 (.a(bit0), .b(bit1), .out(adder_2_out));  // open: cin, cout
  Adder #(.width(4)) adder_3 (.a(bit2), .b(bit3), .out(adder_3_out));  // open: cin, cout
  Adder #(.width(4)) adder_4 (.a(bit4), .b(bit5), .out(adder_4_out));  // open: cin, cout
  Adder #(.width(4)) adder_5 (.a(bit6), .b(bit7), .out(adder_5_out));  // open: cin, cout
  Adder #(.width(4)) adder_6 (.a(bit8), .b(bit9), .out(adder_6_out));  // open: cin, cout
  // Probe on shift_lui
  Multiplexer #(.width(32)) multiplexer_18 (
    .in0(multiplexer_16_out), .in1(r1), .out(multiplexer_18_out), .sel(jr));  // open: en
  // Probe on r1
  and and_10 (and_10_out, comparator_32_eq, Bne);
  Multiplexer #(.width(32)) multiplexer_19 (
    .in0(main_2_result), .in1(main_3_p5), .out(multiplexer_19_out), .sel(MemtoReg));  // open: en
  Multiplexer #(.width(32)) multiplexer_20 (
    .in0(multiplexer_19_out), .in1(FETCH_ADDRESS), .out(multiplexer_20_out), .sel(Jal));  // open: en
  Multiplexer #(.width(32)) multiplexer_21 (
    .in0(bit_extender_2_out), .in1(bit_extender_3_out), .out(Imm), .sel(Extop));  // open: en
  // Probe on actual_instruction[15:11]
  or or_16 (RegWrite, addi, addiu, swinc, lw, andi, Jal, ori, slti, sltiu, lui, Rtype);
  and and_11 (addu, comparator_30_eq, comparator_31_eq);
  and and_12 (\and , comparator_33_eq, comparator_34_eq);
  Comparator #(.width(6)) comparator_37 (
    .a(actual_instruction[31:26]), .b({6{1'b0}}), .eq(comparator_37_eq));  // open: gt, lt
  Comparator #(.width(6)) comparator_38 (
    .a(actual_instruction[5:0]), .b(6'b101011), .eq(comparator_38_eq));  // open: gt, lt
  Comparator #(.width(6)) comparator_39 (
    .a(actual_instruction[31:26]), .b({6{1'b0}}), .eq(comparator_39_eq));  // open: gt, lt
  Comparator #(.width(6)) comparator_40 (
    .a(actual_instruction[5:0]), .b(6'b001000), .eq(comparator_40_eq));  // open: gt, lt
  Adder #(.width(4)) adder_7 (.a(adder_2_out), .b(adder_3_out), .out(adder_7_out));  // open: cin, cout
  Adder #(.width(4)) adder_8 (.a(adder_4_out), .b(adder_5_out), .out(adder_8_out));  // open: cin, cout
  or or_17 (branch, and_8_out, and_10_out);
  // Probe on multiplexer_19_out
  // Probe on FETCH_ADDRESS
  Multiplexer #(.width(5)) multiplexer_22 (
    .in0(actual_instruction[20:16]), .in1(actual_instruction[15:11]), .out(multiplexer_22_out), .sel(RegDst));  // open: en
  and and_13 (sra, comparator_35_eq, comparator_36_eq);
  and and_14 (sltu, comparator_37_eq, comparator_38_eq);
  Multiplexer #(.select(4), .width(4)) multiplexer_23 (
    .in0(4'b0000), .in1(4'b0001), .in2(4'b0010), .in3(4'b0101), .in4(4'b0110), .in5(4'b0111), .in6(4'b1000),
    .in7(4'b1001), .in8(4'b1010), .in9(4'b1011), .in10(4'b1100), .out(switch), .sel(ctr));  // open: in11, in12, in13, in14, in15, en
  Adder #(.width(4)) adder_9 (.a(adder_7_out), .b(adder_8_out), .out(adder_9_out));  // open: cin, cout
  // Probe on Imm
  Multiplexer #(.width(5)) multiplexer_24 (
    .in0(multiplexer_22_out), .in1({5{1'b1}}), .out(multiplexer_24_out), .sel(Jal));  // open: en
  and and_15 (RegDst, Rtype, 1'b1);
  and and_16 (jr, comparator_39_eq, comparator_40_eq);
  Multiplexer #(.width(5)) multiplexer_25 (
    .in0(multiplexer_24_out), .in1(actual_instruction[25:21]), .out(write_reg), .sel(swinc));  // open: en
  Adder #(.width(4)) adder_10 (.a(adder_9_out), .b(adder_6_out), .out(adder_10_out));  // open: cin, cout
  Adder #(.width(4)) adder_11 (.a(adder_10_out), .b(bit10), .out(ctr));  // open: cin, cout
  assign bit_extender_4_out = {{28{1'b0}}, FETCH_ADDRESS[31:28]};  // Bit_Extender bit_extender_4
  Shifter #(.width(32)) shifter_1 (.in(Imm), .\dist (5'b00010), .out(shifter_1_out));
  assign bit_extender_5_out = {{6{1'b0}}, actual_instruction[25:0]};  // Bit_Extender bit_extender_5
  Shifter #(.width(32)) shifter_2 (.in(bit_extender_4_out), .\dist (5'b11100), .out(shifter_2_out));
  Adder #(.width(32)) adder_12 (.a(shifter_1_out), .b(FETCH_ADDRESS), .out(branchTo));  // open: cin, cout
  or or_18 (Extop, addi, addiu, slti, sltiu);
  Shifter #(.width(32)) shifter_3 (.in(bit_extender_5_out), .\dist (5'b00010), .out(shifter_3_out));
  Adder #(.width(32)) adder_13 (.a(shifter_3_out), .b(shifter_2_out), .out(jp_address));  // open: cin, cout
  or or_19 (kill, branch, jr, Jump);

  // Other names for the same wires on the sheet: func[5:0] = actual_instruction[5:0];
  //   rd[4:0] = actual_instruction[15:11]; rt[4:0] = actual_instruction[20:16]; rs[4:0] = actual_instruction[25:21];
  //   opcode_control[5:0] = actual_instruction[31:26]; clk = CLOCK; fetch_addr[31:0] = FETCH_ADDRESS;
  //   PC_4[31:0] = FETCH_ADDRESS; ra[31:0] = ra_Value; s0[31:0] = s0_Value; s1[31:0] = s1_Value; s2[31:0] = s2_Value;
  //   sp[31:0] = sp_Value

  // Notes on the sheet:
  //   Output
  //   These are outputs/inputs from run.circ
  //   Inputs
  //   These are DEBUG/TEST outputs from your circuit.
endmodule
