// Logisim project alu.circ as structural Verilog: 1 circuit, main circuit main
module main (
  input  [31:0] X,
  input  [31:0] Y,
  input  [3:0] Switch,
  output Signed_Overflow,
  output Equal,
  output [31:0] Result
);

  wire _31th_carryin, _31th_carryout, add_overflow, adder_1_cout, adder_1_out, and_1_out, and_2_out,
       comparator_1_lt, comparator_4_eq, comparator_5_eq, not_1_out, not_2_out, not_3_out, signedgreater,
       signedless, sub_overflow, unsigngreater, unsignless;
  wire [4:0] bit_extender_1_out;
  wire [31:0] add, addu, \and , arithmatic_right_shift, left_shift, \or , right_shift, slt, sltu, sub, subu;

  Adder #(.width(1)) adder_1 (.a(X[30]), .b(Y[30]), .out(adder_1_out), .cout(adder_1_cout));  // open: cin
  Adder #(.width(1)) adder_2 (.a(Y[31]), .b(X[31]), .cin(_31th_carryin), .cout(_31th_carryout));  // open: out
  Comparator #(.width(1), .mode("unsigned")) comparator_1 (
    .a(add[30]), .b(adder_1_out), .lt(comparator_1_lt));  // open: gt, eq
  or or_1 (_31th_carryin, comparator_1_lt, adder_1_cout);
  xor xor_1 (add_overflow, _31th_carryout, _31th_carryin);
  Multiplexer #(.select(4)) multiplexer_1 (
    .in0(1'b0), .in1(1'b0), .in2(1'b0), .in3(1'b0), .in4(1'b0), .in5(add_overflow), .in6(1'b0),
    .in7(sub_overflow), .in8(1'b0), .in9(1'b0), .in10(1'b0), .in11(1'b0), .in12(1'b0), .in13(1'b0),
    .in14(1'b0), .in15(1'b0), .out(Signed_Overflow), .sel(Switch));  // open: en
  Bit_Extender #(.in_width(32), .out_width(5)) bit_extender_1 (.in(X), .out(bit_extender_1_out));
  not not_1 (not_1_out, signedgreater);
  and and_1 (and_1_out, not_1_out, signedless);
  not not_2 (not_2_out, unsigngreater);
  assign slt = {{31{1'b0}}, and_1_out};  // Bit_Extender bit_extender_2
  and and_2 (and_2_out, not_2_out, unsignless);
  Shifter #(.width(32)) shifter_1 (.in(Y), .\dist (bit_extender_1_out), .out(left_shift));
  Shifter #(.width(32), .shift("lr")) shifter_2 (.in(Y), .\dist (bit_extender_1_out), .out(right_shift));
  Shifter #(.width(32), .shift("ar")) shifter_3 (.in(Y), .\dist (bit_extender_1_out), .out(arithmatic_right_shift));
  Adder #(.width(32)) adder_3 (.a(X), .b(Y), .out(add));  // open: cin, cout
  Adder #(.width(32)) adder_4 (.a(X), .b(Y), .out(addu));  // open: cin, cout
  Subtractor #(.width(32)) subtractor_1 (.a(X), .b(Y), .out(sub));  // open: bin, bout
  Subtractor #(.width(32)) subtractor_2 (.a(X), .b(Y), .out(subu));  // open: bin, bout
  assign \and  = X & Y;  // AND_Gate and_3, 32 bits wide
  assign \or  = X | Y;  // OR_Gate or_2, 32 bits wide
  Comparator #(.width(32)) comparator_2 (.a(X), .b(Y), .gt(signedgreater), .eq(Equal), .lt(signedless));
  Comparator #(.width(32), .mode("unsigned")) comparator_3 (
    .a(X), .b(Y), .gt(unsigngreater), .eq(Equal), .lt(unsignless));
  assign sltu = {{31{1'b0}}, and_2_out};  // Bit_Extender bit_extender_3
  Comparator #(.width(1)) comparator_4 (.a(X[31]), .b(Y[31]), .eq(comparator_4_eq));  // open: gt, lt
  not not_3 (not_3_out, comparator_4_eq);
  Comparator #(.width(1)) comparator_5 (.a(sub[31]), .b(Y[31]), .eq(comparator_5_eq));  // open: gt, lt
  and and_4 (sub_overflow, not_3_out, comparator_5_eq);
  Multiplexer #(.select(4), .width(32)) multiplexer_2 (
    .in0(left_shift), .in1(right_shift), .in2(arithmatic_right_shift), .in5(add), .in6(addu), .in7(sub),
    .in8(subu), .in9(\and ), .in10(\or ), .in11(slt), .in12(sltu), .out(Result), .sel(Switch));  // open: in3, in4, in13, in14, in15, en

  // Other names for the same wires on the sheet: overflow = Signed_Overflow; S[3:0] = Switch

  // Notes on the sheet:
  //   INPUTS to your circuit
  //   DON'T CHANGE THE LOCATIONS OF THE INPUTS AND OUTPUTS!
  //   OUTPUTS from your circuit
endmodule
