// Logisim project regfile.circ as structural Verilog: 1 circuit, main circuit main
module main (
  input  [4:0] Read_Register_1,
  input  [4:0] Read_Register_2,
  input  [4:0] Write_Register,
  input  [31:0] Write_Data,
  input  Write_Enable,
  input  Clock,
  output [31:0] s0_Value,
  output [31:0] s1_Value,
  output [31:0] s2_Value,
  output [31:0] ra_Value,
  output [31:0] sp_Value,
  output [31:0] Read_Data_1,
  output [31:0] Read_Data_2
);

  wire demultiplexer_2_out1, demultiplexer_2_out2, demultiplexer_2_out3, demultiplexer_2_out4,
       demultiplexer_2_out5, demultiplexer_2_out6, demultiplexer_2_out7, demultiplexer_2_out8,
       demultiplexer_2_out9, demultiplexer_2_out10, demultiplexer_2_out11, demultiplexer_2_out12,
       demultiplexer_2_out13, demultiplexer_2_out14, demultiplexer_2_out15, demultiplexer_2_out16,
       demultiplexer_2_out17, demultiplexer_2_out18, demultiplexer_2_out19, demultiplexer_2_out20,
       demultiplexer_2_out21, demultiplexer_2_out22, demultiplexer_2_out23, demultiplexer_2_out24,
       demultiplexer_2_out25, demultiplexer_2_out26, demultiplexer_2_out27, demultiplexer_2_out28,
       demultiplexer_2_out29, demultiplexer_2_out30, demultiplexer_2_out31;
  wire [31:0] a0, a0w, a1, a1w, a2, a2w, a3, a3w, at, atw, fp, fpw, gp, gpw, k0, k0w, k1, k1w, raw, s0w, s1w,
       s2w, s3, s3w, s4, s4w, s5, s5w, s6, s6w, s7, s7w, spw, t0, t0w, t1, t1w, t2, t2w, t3, t3w, t4, t4w,
       t5, t5w, t6, t6w, t7, t7w, t8, t8w, t9, t9w, v0, v0w, v1, v1w;

  Demultiplexer #(.select(5), .width(32)) demultiplexer_1 (
    .out1(atw), .out2(v0w), .out3(v1w), .out4(a0w), .out5(a1w), .out6(a2w), .out7(a3w), .out8(t0w),
    .out9(t1w), .out10(t2w), .out11(t3w), .out12(t4w), .out13(t5w), .out14(t6w), .out15(t7w), .out16(s0w),
    .out17(s1w), .out18(s2w), .out19(s3w), .out20(s4w), .out21(s5w), .out22(s6w), .out23(s7w), .out24(t8w),
    .out25(t9w), .out26(k0w), .out27(k1w), .out28(gpw), .out29(spw), .out30(fpw), .out31(raw),
    .in(Write_Data), .sel(Write_Register));  // open: out0, en
  Demultiplexer #(.select(5)) demultiplexer_2 (
    .out1(demultiplexer_2_out1), .out2(demultiplexer_2_out2), .out3(demultiplexer_2_out3),
    .out4(demultiplexer_2_out4), .out5(demultiplexer_2_out5), .out6(demultiplexer_2_out6),
    .out7(demultiplexer_2_out7), .out8(demultiplexer_2_out8), .out9(demultiplexer_2_out9),
    .out10(demultiplexer_2_out10), .out11(demultiplexer_2_out11), .out12(demultiplexer_2_out12),
    .out13(demultiplexer_2_out13), .out14(demultiplexer_2_out14), .out15(demultiplexer_2_out15),
    .out16(demultiplexer_2_out16), .out17(demultiplexer_2_out17), .out18(demultiplexer_2_out18),
    .out19(demultiplexer_2_out19), .out20(demultiplexer_2_out20), .out21(demultiplexer_2_out21),
    .out22(demultiplexer_2_out22), .out23(demultiplexer_2_out23), .out24(demultiplexer_2_out24),
    .out25(demultiplexer_2_out25), .out26(demultiplexer_2_out26), .out27(demultiplexer_2_out27),
    .out28(demultiplexer_2_out28), .out29(demultiplexer_2_out29), .out30(demultiplexer_2_out30),
    .out31(demultiplexer_2_out31), .in(Write_Enable), .sel(Write_Register));  // open: out0, en
  Multiplexer #(.select(5), .width(32)) multiplexer_1 (
    .in0({32{1'b0}}), .in1(at), .in2(v0), .in3(v1), .in4(a0), .in5(a1), .in6(a2), .in7(a3), .in8(t0),
    .in9(t1), .in10(t2), .in11(t3), .in12(t4), .in13(t5), .in14(t6), .in15(t7), .in16(s0_Value),
    .in17(s1_Value), .in18(s2_Value), .in19(s3), .in20(s4), .in21(s5), .in22(s6), .in23(s7), .in24(t8),
    .in25(t9), .in26(k0), .in27(k1), .in28(gp), .in29(sp_Value), .in30(fp), .in31(ra_Value),
    .out(Read_Data_1), .sel(Read_Register_1));  // open: en
  Register #(.width(32)) register_1 (.D(spw), .en(demultiplexer_2_out29), .Q(sp_Value), .clk(Clock));  // open: clr
  Register #(.width(32)) register_2 (.D(s1w), .en(demultiplexer_2_out17), .Q(s1_Value), .clk(Clock));  // open: clr
  Register #(.width(32)) register_3 (.D(s2w), .en(demultiplexer_2_out18), .Q(s2_Value), .clk(Clock));  // open: clr
  Register #(.width(32)) register_4 (.D(s3w), .en(demultiplexer_2_out19), .Q(s3), .clk(Clock));  // open: clr
  Register #(.width(32)) register_5 (.D(s4w), .en(demultiplexer_2_out20), .Q(s4), .clk(Clock));  // open: clr
  Register #(.width(32)) register_6 (.D(s5w), .en(demultiplexer_2_out21), .Q(s5), .clk(Clock));  // open: clr
  Register #(.width(32)) register_7 (.D(s6w), .en(demultiplexer_2_out22), .Q(s6), .clk(Clock));  // open: clr
  Register #(.width(32)) register_8 (.D(s7w), .en(demultiplexer_2_out23), .Q(s7), .clk(Clock));  // open: clr
  Register #(.width(32)) register_9 (.D(t8w), .en(demultiplexer_2_out24), .Q(t8), .clk(Clock));  // open: clr
  Register #(.width(32)) register_10 (.D(t9w), .en(demultiplexer_2_out25), .Q(t9), .clk(Clock));  // open: clr
  Register #(.width(32)) register_11 (.D(k1w), .en(demultiplexer_2_out27), .Q(k1), .clk(Clock));  // open: clr
  Register #(.width(32)) register_12 (.D(fpw), .en(demultiplexer_2_out30), .Q(fp), .clk(Clock));  // open: clr
  Register #(.width(32)) register_13 (.D(atw), .en(demultiplexer_2_out1), .Q(at), .clk(Clock));  // open: clr
  Register #(.width(32)) register_14 (.D(v0w), .en(demultiplexer_2_out2), .Q(v0), .clk(Clock));  // open: clr
  Register #(.width(32)) register_15 (.D(v1w), .en(demultiplexer_2_out3), .Q(v1), .clk(Clock));  // open: clr
  Register #(.width(32)) register_16 (.D(a0w), .en(demultiplexer_2_out4), .Q(a0), .clk(Clock));  // open: clr
  Register #(.width(32)) register_17 (.D(a1w), .en(demultiplexer_2_out5), .Q(a1), .clk(Clock));  // open: clr
  Register #(.width(32)) register_18 (.D(a2w), .en(demultiplexer_2_out6), .Q(a2), .clk(Clock));  // open: clr
  Register #(.width(32)) register_19 (.D(a3w), .en(demultiplexer_2_out7), .Q(a3), .clk(Clock));  // open: clr
  Register #(.width(32)) register_20 (.D(t0w), .en(demultiplexer_2_out8), .Q(t0), .clk(Clock));  // open: clr
  Register #(.width(32)) register_21 (.D(t1w), .en(demultiplexer_2_out9), .Q(t1), .clk(Clock));  // open: clr
  Register #(.width(32)) register_22 (.D(t2w), .en(demultiplexer_2_out10), .Q(t2), .clk(Clock));  // open: clr
  Register #(.width(32)) register_23 (.D(t3w), .en(demultiplexer_2_out11), .Q(t3), .clk(Clock));  // open: clr
  Register #(.width(32)) register_24 (.D(t4w), .en(demultiplexer_2_out12), .Q(t4), .clk(Clock));  // open: clr
  Register #(.width(32)) register_25 (.D(t5w), .en(demultiplexer_2_out13), .Q(t5), .clk(Clock));  // open: clr
  Register #(.width(32)) register_26 (.D(t6w), .en(demultiplexer_2_out14), .Q(t6), .clk(Clock));  // open: clr
  Register #(.width(32)) register_27 (.D(t7w), .en(demultiplexer_2_out15), .Q(t7), .clk(Clock));  // open: clr
  Register #(.width(32)) register_28 (.D(s0w), .en(demultiplexer_2_out16), .Q(s0_Value), .clk(Clock));  // open: clr
  Register #(.width(32)) register_29 (.D(k0w), .en(demultiplexer_2_out26), .Q(k0), .clk(Clock));  // open: clr
  Register #(.width(32)) register_30 (.D(gpw), .en(demultiplexer_2_out28), .Q(gp), .clk(Clock));  // open: clr
  Register #(.width(32)) register_31 (.D(raw), .en(demultiplexer_2_out31), .Q(ra_Value), .clk(Clock));  // open: clr
  Multiplexer #(.select(5), .width(32)) multiplexer_2 (
    .in0({32{1'b0}}), .in1(at), .in2(v0), .in3(v1), .in4(a0), .in5(a1), .in6(a2), .in7(a3), .in8(t0),
    .in9(t1), .in10(t2), .in11(t3), .in12(t4), .in13(t5), .in14(t6), .in15(t7), .in16(s0_Value),
    .in17(s1_Value), .in18(s2_Value), .in19(s3), .in20(s4), .in21(s5), .in22(s6), .in23(s7), .in24(t8),
    .in25(t9), .in26(k0), .in27(k1), .in28(gp), .in29(sp_Value), .in30(fp), .in31(ra_Value),
    .out(Read_Data_2), .sel(Read_Register_2));  // open: en

  // Other names for the same wires on the sheet: clk = Clock; ra[31:0] = ra_Value; read_data1[31:0] = Read_Data_1;
  //   read_data2[31:0] = Read_Data_2; read_reg1[4:0] = Read_Register_1; read_reg2[4:0] = Read_Register_2;
  //   s0[31:0] = s0_Value; s1[31:0] = s1_Value; s2[31:0] = s2_Value; sp[31:0] = sp_Value; write_en = Write_Enable;
  //   write_reg[4:0] = Write_Register

  // Notes on the sheet:
  //   INPUTS to your circuit
  //   DON'T CHANGE THE LOCATIONS OF THE INPUTS AND OUTPUTS!
  //   These are DEBUG/TEST outputs from your circuit.
  //   OUTPUTS from your circuit
endmodule
